# Fritzing sketch game8266_SPI (saved by Fritzing 0.9.3b)
circuit board: 8.46667cm x 5.64444cm

parts:
  SW2 = IC, DIP package, 4 pins [chip_label=U]
  IC11 = DIP - 4 pins [chip_label=L package="DIP (Dual Inline) [THT]"]
  IC12 = DIP - 4 pins [chip_label=R package="DIP (Dual Inline) [THT]"]
  IC13 = DIP - 4 pins [chip_label=D package="DIP (Dual Inline) [THT]"]
  IC14 = DIP - 4 pins [chip_label=A package="DIP (Dual Inline) [THT]"]
  IC15 = DIP - 4 pins [chip_label=B package="DIP (Dual Inline) [THT]"]
  Piezo_Speaker = Piezo Speaker - PC Mount [part_number=COM-07950]
  R1 = Resistor [tolerance=±5% resistance=15k package=THT]  # not connected
  R = Resistor [tolerance=±5% resistance=10k package=THT]  # not connected
  R4 = Resistor [tolerance=±5% resistance=10k package=THT]  # not connected
  WeMos_D1_Mini4 = WeMos D1 Mini
  R5 = Resistor [tolerance=±5% resistance=10k package=THT]  # not connected
  R6 = Resistor [tolerance=±5% resistance=15k package=THT]  # not connected
  R7 = Resistor [tolerance=±5% resistance=10k package=THT]
  D1 = Diode [package=diode-hv]
  R8 = Resistor [tolerance=±5% resistance=10k package=THT]
  R9 = Trimmer Potentiometer [maximum_resistance=10kΩ package=THT]
  D2 = Diode [package=diode-hv]
  OLED2 = 128x64 Monochrom OLED Display with SPI Control
  R10 = Trimmer Potentiometer [maximum_resistance=10kΩ package=THT]
  D3 = Diode [package=diode-hv]

nets:
  N1: SW2.pin2, IC13.pin3
  N2: IC11.pin2, IC12.pin1, IC13.pin2, IC14.pin2, IC15.pin2
  N3: IC14.pin3, D1.A
  GND: Piezo_Speaker.GND, WeMos_D1_Mini4.G, R7.Pin_0, R9.leg1, OLED2.GND, R10.leg1
  N4: Piezo_Speaker.VCC, WeMos_D1_Mini4.D8
  3V3: WeMos_D1_Mini4.3V3, OLED2.3v3
  N5: WeMos_D1_Mini4.A0, D1.C, D2.C, D3.C
  N6: WeMos_D1_Mini4.D0, OLED2.Reset
  N7: WeMos_D1_Mini4.D1, R8.Pin_0
  N8: WeMos_D1_Mini4.D2, R10.leg2
  N9: WeMos_D1_Mini4.D3, R9.leg2
  N10: WeMos_D1_Mini4.D4, OLED2.SA0/DC
  N11: WeMos_D1_Mini4.D5, OLED2.Clock
  N12: WeMos_D1_Mini4.D7, OLED2.Data
  N13: R10.wiper, D3.A

notes:
  ESP8266 Micropython game console
  cheungbx 2019-09-17
  pin layout for
  Node MCU D1 Mini
  # SPI OLED
  # SSD1306 # ESP8266
  # GND -------- GND
  # VCC --------- VCC
  # D0/Sck ------ D5 (=GPIO14=HSCLK)
  # D1/MOSI---- D7 (=GPIO13=HMOSI)
  # RES ----------- D0 (=GPIO16)
  # DC ----------- D4 (=GPIO2)
  # CS ------------ GND
  # Speaker+ ---GPIO15/ D8
  # Speaker- ----GND
  # n.c. --------- D6 (=GPIO13=HMOSI)
  #
  # GPIO5 D1—— On to read ADC for Btn /I2C SCL
  # GPIO4 D2—— On to read ADC for Paddle / I2C SDA
  # GPIO0 D3—— On to read ADC for Paddle2
  # ADC (0) - A0 --Diode 1N4148-- Buttons (10K VR),
  # ADC (0) - A0 -- Diode 1N4148 - Paddle1 (10K VR)
  # ADC (0) - A0 -- Diode 1N4148 - Paddle2 (10K VR)
  # VCC-9K-U-9K-L-12K-R-9K-D-9K-A-12K-B-9K-GND

custom parts:
  DIP - 4 pins: A DIP stand-in part for whatever IC you want. With 4 pins on a 300mil dual inline package (DIP) footprint.
  Piezo Speaker - PC Mount: This is a small 12mm round speaker that operates around the audible 2kHz range. You can use these speakers to create simple music or user interfaces. Each speaker is PTH solderable and requires an operating voltage of 3.5-5V with a mean current of 35mA max. These speakers also have a typical sound output of 95 dBA and a coil resistance of 42 ±6.3 ohms.
